// Logisim project DirectionChange.circ as structural Verilog: 1 circuit, main circuit main
module main (
);

  wire and_1_out, clock_1_out, d_ff_1_q, d_ff_1_qn, d_ff_2_q, d_ff_2_qn, d_ff_3_q, d_ff_3_qn, d_ff_4_q,
       d_ff_4_qn, d_ff_5_q, d_ff_5_qn, nand_1_out, nand_2_out, nand_3_out, nand_4_out, nand_5_out,
       nand_6_out, nand_7_out, nand_8_out, nand_9_out, nand_10_out, nand_11_out, nand_12_out, nand_13_out,
       nand_14_out, nand_15_out, nand_16_out, nand_17_out, nand_18_out, nand_19_out, nand_20_out,
       nand_21_out, nand_22_out, nand_23_out, nand_24_out, nand_25_out, nand_26_out, nand_27_out,
       nand_28_out, nor_1_out, nor_2_out, nor_3_out, nor_4_out, nor_5_out, nor_6_out, nor_7_out, nor_8_out,
       nor_9_out, nor_10_out, or_1_out;

  Clock clock_1 (.out(clock_1_out));
  or or_1 (or_1_out, d_ff_3_q, d_ff_1_q);
  and and_1 (and_1_out, or_1_out, d_ff_2_q);
  D_Flip_Flop d_ff_1 (
    .clk(clock_1_out), .D(d_ff_5_qn), .Q(d_ff_1_q), .Qn(d_ff_1_qn), .reset(nor_10_out));  // open: preset, en
  D_Flip_Flop d_ff_2 (
    .clk(clock_1_out), .D(d_ff_1_q), .Q(d_ff_2_q), .Qn(d_ff_2_qn), .reset(nor_10_out));  // open: preset, en
  D_Flip_Flop d_ff_3 (
    .clk(clock_1_out), .D(and_1_out), .Q(d_ff_3_q), .Qn(d_ff_3_qn), .reset(nor_10_out));  // open: preset, en
  D_Flip_Flop d_ff_4 (
    .clk(clock_1_out), .D(d_ff_3_q), .Q(d_ff_4_q), .Qn(d_ff_4_qn), .reset(nor_10_out));  // open: preset, en
  D_Flip_Flop d_ff_5 (
    .clk(clock_1_out), .D(d_ff_4_q), .Q(d_ff_5_q), .Qn(d_ff_5_qn), .reset(nor_10_out));  // open: preset, en
  nor nor_1 (nor_1_out, d_ff_5_q, d_ff_1_q);
  nor nor_2 (nor_2_out, d_ff_2_q, d_ff_1_qn);
  nor nor_3 (nor_3_out, d_ff_2_qn, d_ff_3_q);
  nor nor_4 (nor_4_out, d_ff_4_q, d_ff_3_qn);
  nor nor_5 (nor_5_out, d_ff_5_q, d_ff_4_qn);
  nor nor_6 (nor_6_out, d_ff_1_qn, d_ff_5_qn);
  nor nor_7 (nor_7_out, d_ff_1_q, d_ff_2_qn);
  nor nor_8 (nor_8_out, d_ff_2_q, d_ff_3_qn);
  nor nor_9 (nor_9_out, d_ff_4_qn, d_ff_3_q);
  nor nor_10 (nor_10_out, d_ff_4_q, d_ff_5_qn);
  // Probe on nand_1_out
  nand nand_1 (nand_1_out, 1'b1, 1'b1);
  nand nand_2 (nand_2_out, nand_1_out, nor_1_out);
  nand nand_3 (nand_3_out, 1'b1, nor_9_out);
  nand nand_4 (nand_4_out, nand_1_out, nor_2_out);
  nand nand_5 (nand_5_out, 1'b1, nor_8_out);
  nand nand_6 (nand_6_out, nand_1_out, nor_3_out);
  nand nand_7 (nand_7_out, 1'b1, nor_7_out);
  nand nand_8 (nand_8_out, nand_1_out, nor_4_out);
  nand nand_9 (nand_9_out, 1'b1, nor_6_out);
  nand nand_10 (nand_10_out, nand_1_out, nor_5_out);
  nand nand_11 (nand_11_out, 1'b1, nor_5_out);
  nand nand_12 (nand_12_out, nand_1_out, nor_6_out);
  nand nand_13 (nand_13_out, 1'b1, nor_4_out);
  nand nand_14 (nand_14_out, nand_1_out, nor_7_out);
  nand nand_15 (nand_15_out, 1'b1, nor_3_out);
  nand nand_16 (nand_16_out, nand_1_out, nor_8_out);
  nand nand_17 (nand_17_out, 1'b1, nor_2_out);
  nand nand_18 (nand_18_out, nand_1_out, nor_9_out);
  nand nand_19 (nand_19_out, 1'b1, nor_1_out);
  nand nand_20 (nand_20_out, nand_2_out, nand_3_out);
  // Probe on nand_20_out
  nand nand_21 (nand_21_out, nand_4_out, nand_5_out);
  // Probe on nand_21_out
  nand nand_22 (nand_22_out, nand_6_out, nand_7_out);
  // Probe on nand_22_out
  // Probe on nand_23_out
  nand nand_23 (nand_23_out, nand_8_out, nand_9_out);
  // Probe on nand_24_out
  nand nand_24 (nand_24_out, nand_10_out, nand_11_out);
  nand nand_25 (nand_25_out, nand_12_out, nand_13_out);
  // Probe on nand_25_out
  nand nand_26 (nand_26_out, nand_14_out, nand_15_out);
  // Probe on nand_26_out
  nand nand_27 (nand_27_out, nand_16_out, nand_17_out);
  // Probe on nand_27_out
  nand nand_28 (nand_28_out, nand_18_out, nand_19_out);
  // Probe on nand_28_out

  // Notes on the sheet:
  //   Mr
  //   Q0
  //   Q1
  //   Q2
  //   Q3
  //   Q4
  //   Q5
  //   Q6
  //   Q7
  //   Q8
  //   Q9
  //   DIR
  //   DIR/
endmodule
