// Logisim project JohnsonCounterDirectionChange.circ as structural Verilog: 1 circuit, main circuit main
module main (
);

  wire clock_1_out, j_k_ff_1_q, j_k_ff_1_qn, j_k_ff_2_q, j_k_ff_2_qn, j_k_ff_3_q, j_k_ff_3_qn, j_k_ff_4_q,
       j_k_ff_4_qn, j_k_ff_5_q, j_k_ff_5_qn, nand_1_out, nand_2_out, nand_3_out, nand_4_out, nand_5_out,
       nand_6_out, nand_7_out, nand_8_out, nand_9_out, nand_10_out, nand_11_out, nand_12_out, nand_13_out,
       nand_14_out, nand_15_out, nand_16_out, nand_17_out, nand_18_out, nand_19_out, nand_20_out,
       nand_21_out, nand_22_out, nand_23_out, nand_24_out, nand_25_out, nand_26_out, nand_27_out, nand_28_out;

  Clock clock_1 (.out(clock_1_out));
  J_K_Flip_Flop j_k_ff_1 (
    .J(j_k_ff_5_qn), .clk(clock_1_out), .K(j_k_ff_5_q), .Q(j_k_ff_1_q), .Qn(j_k_ff_1_qn));  // open: preset, en, reset
  J_K_Flip_Flop j_k_ff_2 (
    .J(j_k_ff_1_q), .clk(clock_1_out), .K(j_k_ff_1_qn), .Q(j_k_ff_2_q), .Qn(j_k_ff_2_qn));  // open: preset, en, reset
  J_K_Flip_Flop j_k_ff_3 (
    .J(j_k_ff_2_q), .clk(clock_1_out), .K(j_k_ff_2_qn), .Q(j_k_ff_3_q), .Qn(j_k_ff_3_qn));  // open: preset, en, reset
  J_K_Flip_Flop j_k_ff_4 (
    .J(j_k_ff_3_q), .clk(clock_1_out), .K(j_k_ff_3_qn), .Q(j_k_ff_4_q), .Qn(j_k_ff_4_qn));  // open: preset, en, reset
  J_K_Flip_Flop j_k_ff_5 (
    .J(j_k_ff_4_q), .clk(clock_1_out), .K(j_k_ff_4_qn), .Q(j_k_ff_5_q), .Qn(j_k_ff_5_qn));  // open: preset, en, reset
  // Probe on nand_1_out
  nand nand_1 (nand_1_out, 1'b0, 1'b0);
  nand nand_2 (nand_2_out, nand_1_out, j_k_ff_1_q);
  nand nand_3 (nand_3_out, 1'b0, j_k_ff_5_qn);
  nand nand_4 (nand_4_out, nand_1_out, j_k_ff_2_q);
  nand nand_5 (nand_5_out, 1'b0, j_k_ff_4_qn);
  nand nand_6 (nand_6_out, nand_1_out, j_k_ff_3_q);
  nand nand_7 (nand_7_out, 1'b0, j_k_ff_3_qn);
  nand nand_8 (nand_8_out, nand_1_out, j_k_ff_4_q);
  nand nand_9 (nand_9_out, 1'b0, j_k_ff_2_qn);
  nand nand_10 (nand_10_out, nand_1_out, j_k_ff_1_qn);
  nand nand_11 (nand_11_out, 1'b0, j_k_ff_1_qn);
  nand nand_12 (nand_12_out, nand_1_out, j_k_ff_2_qn);
  nand nand_13 (nand_13_out, 1'b0, j_k_ff_4_q);
  nand nand_14 (nand_14_out, nand_1_out, j_k_ff_3_qn);
  nand nand_15 (nand_15_out, 1'b0, j_k_ff_3_q);
  nand nand_16 (nand_16_out, nand_1_out, j_k_ff_4_qn);
  nand nand_17 (nand_17_out, 1'b0, j_k_ff_2_q);
  nand nand_18 (nand_18_out, nand_1_out, j_k_ff_5_qn);
  nand nand_19 (nand_19_out, 1'b0, j_k_ff_1_q);
  // Probe on nand_20_out
  nand nand_20 (nand_20_out, nand_2_out, nand_3_out);
  nand nand_21 (nand_21_out, nand_4_out, nand_5_out);
  // Probe on nand_21_out
  nand nand_22 (nand_22_out, nand_6_out, nand_7_out);
  // Probe on nand_22_out
  nand nand_23 (nand_23_out, nand_8_out, nand_9_out);
  // Probe on nand_23_out
  nand nand_24 (nand_24_out, nand_10_out, nand_11_out);
  // Probe on nand_24_out
  nand nand_25 (nand_25_out, nand_12_out, nand_13_out);
  // Probe on nand_25_out
  nand nand_26 (nand_26_out, nand_14_out, nand_15_out);
  // Probe on nand_26_out
  nand nand_27 (nand_27_out, nand_16_out, nand_17_out);
  // Probe on nand_27_out
  nand nand_28 (nand_28_out, nand_18_out, nand_19_out);
  // Probe on nand_28_out

  // Notes on the sheet:
  //   DIR
  //   DIR/
endmodule
