// Logisim project JohnsonCounterDirectionChangeComplicated.circ as structural Verilog: 1 circuit, main circuit main
module main (
);

  wire clock_1_out, d_ff_1_q, d_ff_1_qn, d_ff_2_q, d_ff_2_qn, d_ff_3_q, d_ff_3_qn, d_ff_4_q, d_ff_4_qn,
       d_ff_5_q, d_ff_5_qn, nand_1_out, nand_2_out, nand_3_out, nand_4_out, nand_5_out, nand_6_out,
       nand_7_out, nand_8_out, nand_9_out, nand_10_out, nand_11_out, nand_12_out, nand_13_out, nand_14_out,
       nand_15_out, nand_16_out, nand_17_out, nand_18_out, nand_19_out, nand_20_out, nand_21_out,
       nand_22_out, nand_23_out, nand_24_out, nand_25_out, nand_26_out, nand_27_out, nand_28_out,
       nand_29_out, nand_30_out, nand_31_out, nand_32_out, nand_33_out, nand_34_out, nand_35_out,
       nand_36_out, nand_37_out;

  // Probe on nand_1_out
  nand nand_1 (nand_1_out, 1'b0, 1'b0);
  Clock clock_1 (.out(clock_1_out));
  // Probe on nand_2_out
  nand nand_2 (nand_2_out, nand_3_out, nand_3_out);
  nand nand_3 (nand_3_out, nand_4_out, nand_5_out);
  // Probe on nand_3_out
  nand nand_4 (nand_4_out, nand_1_out, d_ff_5_qn, d_ff_1_q);
  nand nand_5 (nand_5_out, 1'b0, d_ff_4_qn);
  D_Flip_Flop d_ff_1 (
    .clk(clock_1_out), .D(d_ff_5_qn), .Q(d_ff_1_q), .Qn(d_ff_1_qn), .reset(1'b0));  // open: preset, en
  nand nand_6 (nand_6_out, nand_7_out, nand_7_out);
  // Probe on nand_6_out
  nand nand_7 (nand_7_out, nand_9_out, nand_8_out);
  // Probe on nand_7_out
  nand nand_8 (nand_8_out, 1'b0, d_ff_3_qn);
  nand nand_9 (nand_9_out, nand_1_out, d_ff_1_q, d_ff_2_q);
  D_Flip_Flop d_ff_2 (.clk(clock_1_out), .D(d_ff_1_q), .Q(d_ff_2_q), .Qn(d_ff_2_qn), .reset(1'b0));  // open: preset, en
  nand nand_10 (nand_10_out, nand_11_out, nand_11_out);
  // Probe on nand_10_out
  // Probe on nand_11_out
  nand nand_11 (nand_11_out, nand_12_out, nand_13_out);
  nand nand_12 (nand_12_out, nand_1_out, d_ff_2_q, d_ff_3_q);
  nand nand_13 (nand_13_out, 1'b0, d_ff_2_qn);
  D_Flip_Flop d_ff_3 (.clk(clock_1_out), .D(d_ff_2_q), .Q(d_ff_3_q), .Qn(d_ff_3_qn), .reset(1'b0));  // open: preset, en
  // Probe on nand_14_out
  nand nand_14 (nand_14_out, nand_15_out, nand_15_out);
  // Probe on nand_15_out
  nand nand_15 (nand_15_out, nand_17_out, nand_16_out);
  nand nand_16 (nand_16_out, 1'b0, d_ff_1_qn);
  nand nand_17 (nand_17_out, nand_1_out, d_ff_3_q, d_ff_4_q);
  D_Flip_Flop d_ff_4 (.clk(clock_1_out), .D(d_ff_3_q), .Q(d_ff_4_q), .Qn(d_ff_4_qn), .reset(1'b0));  // open: preset, en
  // Probe on nand_18_out
  nand nand_18 (nand_18_out, nand_19_out, nand_19_out);
  // Probe on nand_19_out
  nand nand_19 (nand_19_out, nand_20_out, nand_22_out);
  nand nand_20 (nand_20_out, nand_1_out, d_ff_4_q, d_ff_5_q);
  nand nand_21 (nand_21_out, nand_1_out, d_ff_1_qn);
  nand nand_22 (nand_22_out, 1'b0, d_ff_5_q);
  D_Flip_Flop d_ff_5 (.clk(clock_1_out), .D(d_ff_4_q), .Q(d_ff_5_q), .Qn(d_ff_5_qn), .reset(1'b0));  // open: preset, en
  nand nand_23 (nand_23_out, nand_24_out, nand_24_out);
  // Probe on nand_23_out
  // Probe on nand_24_out
  nand nand_24 (nand_24_out, nand_21_out, nand_26_out);
  nand nand_25 (nand_25_out, nand_1_out, d_ff_2_qn);
  nand nand_26 (nand_26_out, 1'b0, d_ff_4_q);
  // Probe on nand_27_out
  nand nand_27 (nand_27_out, nand_30_out, nand_30_out);
  nand nand_28 (nand_28_out, nand_29_out, nand_29_out);
  // Probe on nand_28_out
  // Probe on nand_30_out
  // Probe on nand_29_out
  nand nand_29 (nand_29_out, nand_31_out, nand_37_out);
  nand nand_30 (nand_30_out, nand_25_out, nand_32_out);
  nand nand_31 (nand_31_out, nand_1_out, d_ff_3_qn);
  nand nand_32 (nand_32_out, 1'b0, d_ff_3_q);
  nand nand_33 (nand_33_out, nand_34_out, nand_34_out);
  // Probe on nand_33_out
  // Probe on nand_34_out
  nand nand_34 (nand_34_out, nand_35_out, nand_36_out);
  nand nand_35 (nand_35_out, nand_1_out, d_ff_4_qn);
  nand nand_36 (nand_36_out, 1'b0, d_ff_1_q);
  nand nand_37 (nand_37_out, 1'b0, d_ff_2_q);

  // Notes on the sheet:
  //   DIR
  //   DIR/
  //   PreSet
endmodule
