// Logisim project JohnsonCounterDirectionChangeMinimized.circ as structural Verilog: 1 circuit, main circuit main
module main (
);

  wire clock_1_out, d_ff_1_q, d_ff_2_q, d_ff_3_q, d_ff_4_q, d_ff_5_q, d_ff_6_q, d_ff_7_q, d_ff_8_q, d_ff_9_q,
       nand_1_out, nand_2_out, nand_3_out, nand_4_out, nand_5_out, nand_6_out, nand_7_out, nand_8_out,
       nand_9_out, nand_10_out, nand_11_out, nand_12_out, nand_13_out, nand_14_out, nand_15_out, nand_16_out,
       nand_17_out, nand_18_out, nand_19_out, nand_20_out, nand_21_out, nand_22_out, nand_23_out,
       nand_24_out, nand_25_out, nand_26_out, nand_27_out, nand_28_out, nand_29_out, nand_30_out,
       nand_31_out, not_1_out, not_2_out, not_3_out, not_4_out, not_5_out;

  // Probe on nand_1_out
  nand nand_1 (nand_1_out, 1'b0, 1'b0);
  Clock clock_1 (.out(clock_1_out));
  D_Flip_Flop d_ff_1 (.clk(clock_1_out), .D(nand_2_out), .Q(d_ff_1_q), .reset(1'b0));  // open: Qn, preset, en
  // Probe on nand_2_out
  nand nand_2 (nand_2_out, nand_3_out, nand_4_out);
  nand nand_3 (nand_3_out, nand_1_out, d_ff_9_q);
  nand nand_4 (nand_4_out, 1'b0, d_ff_2_q);
  nand nand_5 (nand_5_out, nand_1_out, d_ff_1_q);
  D_Flip_Flop d_ff_2 (.clk(clock_1_out), .D(nand_6_out), .Q(d_ff_2_q), .reset(1'b0));  // open: Qn, preset, en
  // Probe on nand_6_out
  nand nand_6 (nand_6_out, nand_5_out, nand_7_out);
  nand nand_7 (nand_7_out, 1'b0, d_ff_3_q);
  nand nand_8 (nand_8_out, nand_1_out, d_ff_2_q);
  D_Flip_Flop d_ff_3 (.clk(clock_1_out), .D(nand_9_out), .Q(d_ff_3_q), .reset(1'b0));  // open: Qn, preset, en
  // Probe on nand_9_out
  // Probe on nand_10_out
  nand nand_9 (nand_9_out, nand_8_out, nand_11_out);
  nand nand_10 (nand_10_out, nand_12_out, nand_13_out);
  nand nand_11 (nand_11_out, 1'b0, d_ff_4_q);
  nand nand_12 (nand_12_out, nand_1_out, d_ff_3_q);
  D_Flip_Flop d_ff_4 (.clk(clock_1_out), .D(nand_10_out), .Q(d_ff_4_q), .reset(1'b0));  // open: Qn, preset, en
  nand nand_13 (nand_13_out, 1'b0, d_ff_5_q);
  nand nand_14 (nand_14_out, d_ff_4_q, d_ff_4_q);
  nand nand_15 (nand_15_out, nand_14_out, nand_16_out);
  nand nand_16 (nand_16_out, d_ff_9_q, d_ff_9_q);
  nand nand_17 (nand_17_out, nand_18_out, nand_22_out);
  // Probe on nand_17_out
  nand nand_18 (nand_18_out, nand_1_out, d_ff_4_q);
  D_Flip_Flop d_ff_5 (
    .clk(clock_1_out), .D(nand_17_out), .Q(d_ff_5_q), .preset(not_1_out), .reset(1'b0));  // open: Qn, en
  not not_1 (not_1_out, nand_15_out);
  nand nand_19 (nand_19_out, nand_20_out, nand_21_out);
  // Probe on nand_19_out
  nand nand_20 (nand_20_out, nand_1_out, d_ff_5_q);
  nand nand_21 (nand_21_out, 1'b0, d_ff_7_q);
  nand nand_22 (nand_22_out, 1'b0, d_ff_6_q);
  D_Flip_Flop d_ff_6 (
    .clk(clock_1_out), .D(nand_19_out), .Q(d_ff_6_q), .preset(not_2_out), .reset(1'b0));  // open: Qn, en
  not not_2 (not_2_out, nand_15_out);
  not not_3 (not_3_out, nand_15_out);
  // Probe on nand_23_out
  nand nand_23 (nand_23_out, nand_24_out, nand_25_out);
  nand nand_24 (nand_24_out, nand_1_out, d_ff_6_q);
  nand nand_25 (nand_25_out, 1'b0, d_ff_8_q);
  D_Flip_Flop d_ff_7 (
    .clk(clock_1_out), .D(nand_23_out), .Q(d_ff_7_q), .preset(not_3_out), .reset(1'b0));  // open: Qn, en
  not not_4 (not_4_out, nand_15_out);
  // Probe on nand_26_out
  nand nand_26 (nand_26_out, nand_28_out, nand_27_out);
  nand nand_27 (nand_27_out, 1'b0, d_ff_9_q);
  nand nand_28 (nand_28_out, nand_1_out, d_ff_7_q);
  D_Flip_Flop d_ff_8 (
    .clk(clock_1_out), .D(nand_26_out), .Q(d_ff_8_q), .preset(not_4_out), .reset(1'b0));  // open: Qn, en
  not not_5 (not_5_out, nand_15_out);
  nand nand_29 (nand_29_out, nand_31_out, nand_30_out);
  // Probe on nand_29_out
  nand nand_30 (nand_30_out, 1'b0, d_ff_1_q);
  nand nand_31 (nand_31_out, nand_1_out, d_ff_8_q);
  D_Flip_Flop d_ff_9 (
    .clk(clock_1_out), .D(nand_29_out), .Q(d_ff_9_q), .preset(not_5_out), .reset(1'b0));  // open: Qn, en

  // Notes on the sheet:
  //   Clear
  //   DIR/
  //   DIR
endmodule
