// Logisim project RingCounterSerialScheme.circ as structural Verilog: 1 circuit, main circuit main
module main (
);

  wire and_1_out, and_2_out, and_3_out, and_4_out, and_5_out, and_6_out, and_7_out, clock_1_out, d_ff_1_q,
       d_ff_1_qn, d_ff_2_q, d_ff_2_qn, d_ff_3_q, d_ff_3_qn, d_ff_4_q, d_ff_4_qn, d_ff_5_q, d_ff_5_qn,
       d_ff_6_q, d_ff_6_qn, d_ff_7_q, d_ff_7_qn, d_ff_8_q, d_ff_8_qn, d_ff_9_q, d_ff_9_qn, nand_1_out,
       nand_2_out, nand_3_out, nand_4_out, nand_5_out, nand_6_out, nand_7_out, nand_8_out, nand_9_out,
       nand_10_out, nand_11_out, nand_12_out, nand_13_out, nand_14_out, nand_15_out, nand_16_out,
       nand_17_out, nand_18_out, nand_19_out, nand_20_out, nand_21_out, nand_22_out, nand_23_out,
       nand_24_out, nand_25_out, nand_26_out, nand_27_out, nand_28_out, not_1_out, not_2_out, not_3_out,
       not_4_out, not_5_out, not_6_out, not_7_out, not_8_out, not_9_out, not_10_out, not_11_out, not_12_out,
       not_13_out, not_14_out, not_15_out, not_16_out, not_17_out, not_18_out, not_19_out, not_20_out;

  Clock clock_1 (.out(clock_1_out));
  not not_1 (not_1_out, 1'b1);
  // Probe on nand_4_out
  D_Flip_Flop d_ff_1 (
    .clk(clock_1_out), .D(d_ff_1_qn), .Q(d_ff_1_q), .Qn(d_ff_1_qn), .preset(not_1_out), .reset(not_2_out));  // open: en
  not not_2 (not_2_out, 1'b1);
  not not_3 (not_3_out, 1'b1);
  not not_4 (not_4_out, 1'b1);
  // Probe on nand_1_out
  nand nand_1 (nand_1_out, nand_2_out, nand_3_out);
  nand nand_2 (nand_2_out, nand_4_out, and_6_out);
  nand nand_3 (nand_3_out, 1'b0, d_ff_2_q);
  nand nand_4 (nand_4_out, 1'b0, 1'b0);
  D_Flip_Flop d_ff_2 (
    .clk(d_ff_1_q), .D(nand_5_out), .Q(d_ff_2_q), .Qn(d_ff_2_qn), .preset(not_6_out), .reset(not_5_out));  // open: en
  D_Flip_Flop d_ff_3 (
    .clk(d_ff_1_q), .D(nand_1_out), .Q(d_ff_3_q), .Qn(d_ff_3_qn), .preset(not_4_out), .reset(not_3_out));  // open: en
  not not_5 (not_5_out, 1'b1);
  not not_6 (not_6_out, 1'b1);
  nand nand_5 (nand_5_out, nand_8_out, nand_6_out);
  // Probe on nand_5_out
  nand nand_6 (nand_6_out, 1'b0, d_ff_4_q);
  nand nand_7 (nand_7_out, nand_4_out, d_ff_2_q);
  nand nand_8 (nand_8_out, nand_4_out, d_ff_3_q);
  D_Flip_Flop d_ff_4 (
    .clk(d_ff_1_q), .D(nand_9_out), .Q(d_ff_4_q), .Qn(d_ff_4_qn), .preset(not_7_out), .reset(not_8_out));  // open: en
  not not_7 (not_7_out, 1'b1);
  not not_8 (not_8_out, 1'b1);
  and and_1 (and_1_out, d_ff_2_qn, d_ff_3_qn);
  // Probe on nand_9_out
  nand nand_9 (nand_9_out, nand_7_out, nand_10_out);
  nand nand_10 (nand_10_out, 1'b0, d_ff_5_q);
  nand nand_11 (nand_11_out, nand_4_out, d_ff_4_q);
  D_Flip_Flop d_ff_5 (
    .clk(d_ff_1_q), .D(nand_13_out), .Q(d_ff_5_q), .Qn(d_ff_5_qn), .preset(not_9_out), .reset(not_10_out));  // open: en
  not not_9 (not_9_out, 1'b1);
  not not_10 (not_10_out, 1'b1);
  and and_2 (and_2_out, d_ff_4_qn, and_1_out);
  nand nand_12 (nand_12_out, nand_15_out, nand_19_out);
  // Probe on nand_13_out
  // Probe on nand_12_out
  nand nand_13 (nand_13_out, nand_11_out, nand_14_out);
  nand nand_14 (nand_14_out, 1'b0, d_ff_6_q);
  nand nand_15 (nand_15_out, nand_4_out, d_ff_5_q);
  D_Flip_Flop d_ff_6 (
    .clk(d_ff_1_q), .D(nand_12_out), .Q(d_ff_6_q), .Qn(d_ff_6_qn), .preset(not_11_out), .reset(not_12_out));  // open: en
  not not_11 (not_11_out, 1'b1);
  not not_12 (not_12_out, 1'b1);
  and and_3 (and_3_out, d_ff_5_qn, and_2_out);
  nand nand_16 (nand_16_out, nand_18_out, nand_17_out);
  // Probe on nand_16_out
  nand nand_17 (nand_17_out, 1'b0, d_ff_8_q);
  nand nand_18 (nand_18_out, nand_4_out, d_ff_6_q);
  nand nand_19 (nand_19_out, 1'b0, d_ff_7_q);
  D_Flip_Flop d_ff_7 (
    .clk(d_ff_1_q), .D(nand_16_out), .Q(d_ff_7_q), .Qn(d_ff_7_qn), .preset(not_14_out), .reset(not_13_out));  // open: en
  not not_13 (not_13_out, 1'b1);
  not not_14 (not_14_out, 1'b1);
  not not_15 (not_15_out, 1'b1);
  and and_4 (and_4_out, d_ff_6_qn, and_3_out);
  nand nand_20 (nand_20_out, nand_22_out, nand_21_out);
  // Probe on nand_20_out
  nand nand_21 (nand_21_out, 1'b0, d_ff_9_q);
  nand nand_22 (nand_22_out, nand_4_out, d_ff_7_q);
  D_Flip_Flop d_ff_8 (
    .clk(d_ff_1_q), .D(nand_20_out), .Q(d_ff_8_q), .Qn(d_ff_8_qn), .preset(not_15_out), .reset(not_16_out));  // open: en
  not not_16 (not_16_out, 1'b1);
  not not_17 (not_17_out, 1'b1);
  and and_5 (and_5_out, d_ff_7_qn, and_4_out);
  nand nand_23 (nand_23_out, nand_25_out, nand_24_out);
  // Probe on nand_23_out
  nand nand_24 (nand_24_out, 1'b0, and_6_out);
  nand nand_25 (nand_25_out, nand_4_out, d_ff_8_q);
  D_Flip_Flop d_ff_9 (
    .clk(d_ff_1_q), .D(nand_23_out), .Q(d_ff_9_q), .Qn(d_ff_9_qn), .preset(not_17_out), .reset(not_20_out));  // open: en
  not not_18 (not_18_out, 1'b1);
  not not_19 (not_19_out, 1'b1);
  not not_20 (not_20_out, 1'b1);
  and and_6 (and_6_out, d_ff_9_qn, and_7_out);
  and and_7 (and_7_out, d_ff_8_qn, and_5_out);
  // Probe on nand_26_out
  nand nand_26 (nand_26_out, nand_28_out, nand_27_out);
  nand nand_27 (nand_27_out, 1'b0, d_ff_3_q);
  nand nand_28 (nand_28_out, nand_4_out, d_ff_9_q);
  D_Flip_Flop d_ff_10 (.clk(d_ff_1_q), .D(nand_26_out), .preset(not_19_out), .reset(not_18_out));  // open: Q, Qn, en

  // Notes on the sheet:
  //   Preset
  //   Clear
  //   DIR/
  //   DIR
endmodule
