// Logisim project RingCounterSerialScheme_only_nands.circ as structural Verilog: 2 circuits, main circuit main
module main (
);

  wire clock_1_out, d_ff_1_q, d_ff_1_qn, d_ff_2_q, d_ff_3_q, d_ff_4_q, d_ff_5_q, d_ff_6_q, d_ff_7_q,
       d_ff_8_q, d_ff_9_q, nand_1_out, nand_2_out, nand_3_out, nand_4_out, nand_5_out, nand_6_out,
       nand_7_out, nand_8_out, nand_9_out, nand_10_out, nand_11_out, nand_12_out, nand_13_out, nand_14_out,
       nand_15_out, nand_16_out, nand_17_out, nand_18_out, nand_19_out, nand_20_out, nand_21_out,
       nand_22_out, nand_23_out, nand_24_out, nand_25_out, nand_26_out, nand_27_out, nand_28_out,
       nand_29_out, nand_30_out, nand_31_out, nand_32_out, nand_33_out, nand_34_out, nand_35_out, not_1_out,
       not_2_out, not_3_out, not_4_out, not_5_out, not_6_out, not_7_out, not_8_out, not_9_out, not_10_out,
       not_11_out, not_12_out, not_13_out, not_14_out, not_15_out, not_16_out, not_17_out, not_18_out,
       not_19_out, not_20_out;

  Clock clock_1 (.out(clock_1_out));
  not not_1 (not_1_out, 1'b1);
  // Probe on nand_4_out
  D_Flip_Flop d_ff_1 (
    .clk(clock_1_out), .D(d_ff_1_qn), .Q(d_ff_1_q), .Qn(d_ff_1_qn), .preset(not_1_out), .reset(not_3_out));  // open: en
  not not_2 (not_2_out, 1'b1);
  not not_3 (not_3_out, 1'b1);
  not not_4 (not_4_out, 1'b1);
  // Probe on nand_1_out
  nand nand_1 (nand_1_out, nand_3_out, nand_2_out);
  nand nand_2 (nand_2_out, 1'b0, d_ff_3_q);
  nand nand_3 (nand_3_out, nand_4_out, nand_35_out);
  nand nand_4 (nand_4_out, 1'b0, 1'b0);
  D_Flip_Flop d_ff_2 (
    .clk(d_ff_1_q), .D(nand_1_out), .Q(d_ff_2_q), .preset(not_4_out), .reset(not_2_out));  // open: Qn, en
  D_Flip_Flop d_ff_3 (
    .clk(d_ff_1_q), .D(nand_5_out), .Q(d_ff_3_q), .preset(not_6_out), .reset(not_5_out));  // open: Qn, en
  not not_5 (not_5_out, 1'b1);
  not not_6 (not_6_out, 1'b1);
  nand nand_5 (nand_5_out, nand_7_out, nand_8_out);
  // Probe on nand_5_out
  nand nand_6 (nand_6_out, nand_4_out, d_ff_3_q);
  nand nand_7 (nand_7_out, nand_4_out, d_ff_2_q);
  nand nand_8 (nand_8_out, 1'b0, d_ff_4_q);
  D_Flip_Flop d_ff_4 (
    .clk(d_ff_1_q), .D(nand_10_out), .Q(d_ff_4_q), .preset(not_8_out), .reset(not_7_out));  // open: Qn, en
  not not_7 (not_7_out, 1'b1);
  not not_8 (not_8_out, 1'b1);
  nand nand_9 (nand_9_out, d_ff_3_q, d_ff_2_q);
  nand nand_10 (nand_10_out, nand_6_out, nand_12_out);
  // Probe on nand_10_out
  nand nand_11 (nand_11_out, nand_4_out, d_ff_4_q);
  nand nand_12 (nand_12_out, 1'b0, d_ff_5_q);
  D_Flip_Flop d_ff_5 (
    .clk(d_ff_1_q), .D(nand_15_out), .Q(d_ff_5_q), .preset(not_10_out), .reset(not_9_out));  // open: Qn, en
  not not_9 (not_9_out, 1'b1);
  not not_10 (not_10_out, 1'b1);
  nand nand_13 (nand_13_out, d_ff_4_q, nand_9_out);
  // Probe on nand_14_out
  nand nand_14 (nand_14_out, nand_17_out, nand_21_out);
  // Probe on nand_15_out
  nand nand_15 (nand_15_out, nand_11_out, nand_16_out);
  nand nand_16 (nand_16_out, 1'b0, d_ff_6_q);
  nand nand_17 (nand_17_out, nand_4_out, d_ff_5_q);
  D_Flip_Flop d_ff_6 (
    .clk(d_ff_1_q), .D(nand_14_out), .Q(d_ff_6_q), .preset(not_12_out), .reset(not_11_out));  // open: Qn, en
  not not_11 (not_11_out, 1'b1);
  not not_12 (not_12_out, 1'b1);
  nand nand_18 (nand_18_out, d_ff_5_q, nand_13_out);
  nand nand_19 (nand_19_out, nand_20_out, nand_22_out);
  // Probe on nand_19_out
  nand nand_20 (nand_20_out, nand_4_out, d_ff_6_q);
  nand nand_21 (nand_21_out, 1'b0, d_ff_7_q);
  nand nand_22 (nand_22_out, 1'b0, d_ff_8_q);
  D_Flip_Flop d_ff_7 (
    .clk(d_ff_1_q), .D(nand_19_out), .Q(d_ff_7_q), .preset(not_14_out), .reset(not_15_out));  // open: Qn, en
  not not_13 (not_13_out, 1'b1);
  not not_14 (not_14_out, 1'b1);
  not not_15 (not_15_out, 1'b1);
  nand nand_23 (nand_23_out, d_ff_6_q, nand_18_out);
  nand nand_24 (nand_24_out, nand_26_out, nand_25_out);
  // Probe on nand_24_out
  nand nand_25 (nand_25_out, 1'b0, d_ff_9_q);
  nand nand_26 (nand_26_out, nand_4_out, d_ff_7_q);
  D_Flip_Flop d_ff_8 (
    .clk(d_ff_1_q), .D(nand_24_out), .Q(d_ff_8_q), .preset(not_13_out), .reset(not_16_out));  // open: Qn, en
  not not_16 (not_16_out, 1'b1);
  not not_17 (not_17_out, 1'b1);
  nand nand_27 (nand_27_out, d_ff_7_q, nand_23_out);
  // Probe on nand_28_out
  nand nand_28 (nand_28_out, nand_29_out, nand_30_out);
  nand nand_29 (nand_29_out, nand_4_out, d_ff_8_q);
  nand nand_30 (nand_30_out, 1'b0, nand_35_out);
  D_Flip_Flop d_ff_9 (
    .clk(d_ff_1_q), .D(nand_28_out), .Q(d_ff_9_q), .preset(not_17_out), .reset(not_20_out));  // open: Qn, en
  not not_18 (not_18_out, 1'b1);
  not not_19 (not_19_out, 1'b1);
  not not_20 (not_20_out, 1'b1);
  nand nand_31 (nand_31_out, d_ff_8_q, nand_27_out);
  // Probe on nand_32_out
  nand nand_32 (nand_32_out, nand_33_out, nand_34_out);
  nand nand_33 (nand_33_out, nand_4_out, d_ff_9_q);
  nand nand_34 (nand_34_out, 1'b0, d_ff_2_q);
  D_Flip_Flop d_ff_10 (.clk(d_ff_1_q), .D(nand_32_out), .preset(not_19_out), .reset(not_18_out));  // open: Q, Qn, en
  nand nand_35 (nand_35_out, d_ff_9_q, nand_31_out);

  // Notes on the sheet:
  //   Preset
  //   Clear
  //   DIR/
  //   DIR
endmodule

module main2 (
  input  Q0,
  input  Q1,
  input  Q2,
  input  Q3,
  input  Q4,
  input  Q5,
  input  Q6,
  input  Q7,
  input  Q8,
  output Y
);

  wire nand_1_out;

  nand nand_1 (nand_1_out, Q0, Q1, Q2, Q3, Q4, Q5, Q6, Q7, Q8);
  nand nand_2 (Y, nand_1_out, nand_1_out);
endmodule
